# Fritzing sketch Ketosense_0.1 (saved by Fritzing 0.7.12b)
breadboards: 1

parts:
  Arduino1 = Arduino
  U1 = Voltage Regulator - 5V [package="DPak [SMD]"]
  LCD1 = LCD screen
  Power_plug1 = Power plug
  R1 = Trimmer Potentiometer [maximum_resistance=10kΩ package=THT]
  R2 = 10k Ω Resistor [package=THT]
  S1 = Pushbutton [package="[SMD]"]
  S2 = Pushbutton [package=THT]
  R4 = 47k Ω Resistor [package=THT]
  Part1 = Gas Sensor Breakout Board
  R5 = 47k Ω Resistor [package=THT]
  S3 = Pushbutton [package=THT]
  R6 = 47k Ω Resistor [package=THT]  # not connected
  DHT1 = DHT11 Humitidy and Temperature Sensor  # not connected

nets (from the schematic view):
  GND: Arduino1.GND, U1.GND, LCD1.VSS, LCD1.R/W, LCD1.LED-, Power_plug1.GND, R1.leg2, R2.Pin_0, R4.Pin_0, Part1.GND, R5.Pin_0
  N1: Arduino1.D9, S1.Pin_3, S1.Pin_4, R4.Pin_1
  N2: Arduino1.D8, S2.Pin_1, S2.Pin_2, R5.Pin_1
  N3: Arduino1.D7, LCD1.DB7
  N4: Arduino1.D6, LCD1.DB6
  N5: Arduino1.D5, LCD1.DB5
  N6: Arduino1.D4, LCD1.DB4
  N7: Arduino1.D3, LCD1.E
  N8: Arduino1.D2, LCD1.RS
  VIN: Arduino1.VIN, U1.input_voltage, Power_plug1.VCC
  N9: Arduino1.A0, R2.Pin_1, Part1.A1
  N10: U1.output_voltage, LCD1.VDD, LCD1.LED+, R1.leg1, S1.Pin_1, S1.Pin_2, S2.Pin_3, S2.Pin_4, Part1.B1, Part1.H1
  N11: LCD1.V0, R1.wiper
  N12: S3.Pin_1, S3.Pin_2
  N13: S3.Pin_3, S3.Pin_4

custom parts:
  DHT11 Humitidy and Temperature Sensor: DHT11 Humidity and Temperature Sensor
